// Logisim project MIPS.circ as structural Verilog: 3 circuits, main circuit main
module main (
);

  wire ADD_out, BEQ_out, BeqAndZero_out, clock_1_out, demultiplexer_1_out0, demultiplexer_1_out1,
       demultiplexer_1_out2, demultiplexer_1_out3, fourbitadder_1_overflow, fourbitadder_1_zero,
       Imediato_out, LW_out, Reset_out, SW_out, WB_out;
  wire [1:0] IM_data_2, multiplexer_2_out;
  wire [3:0] adder_1_out, fourbitadder_1_s0, MEM_dout, multiplexer_1_out, multiplexer_3_out,
       multiplexer_4_out, multiplexer_5_out, multiplexer_6_out, multiplexer_7_out, not_1_out, not_2_out,
       PC_q, register_1_q, register_2_q, register_3_q, register_4_q;
  wire [7:2] IM_data;

  Register #(.width(4)) PC (.D(adder_1_out), .en(1'b1), .clk(clock_1_out), .Q(PC_q), .clr(Reset_out));
  Adder #(.width(4)) adder_1 (.a(PC_q), .b(multiplexer_1_out), .out(adder_1_out));  // open: cin, cout
  Multiplexer #(.width(4)) multiplexer_1 (
    .in0(4'b0001), .in1(not_1_out), .out(multiplexer_1_out), .sel(BeqAndZero_out));
  assign not_1_out = ~{2'b00, IM_data_2};  // NOT_Gate not_1, 4 bits wide
  ROM #(.addrWidth(4), .misaligned("true")) IM (.addr(PC_q), .data({IM_data, IM_data_2}));
  Button Reset (.out(Reset_out));
  Clock clock_1 (.out(clock_1_out));
  and BeqAndZero (BeqAndZero_out, BEQ_out, fourbitadder_1_zero);
  and ADD (ADD_out, ~IM_data[6], ~IM_data[7]);  // AND_Gate
  and BEQ (BEQ_out, IM_data[6], ~IM_data[7]);  // AND_Gate
  and SW (SW_out, IM_data[6], IM_data[7]);
  and LW (LW_out, ~IM_data[6], IM_data[7]);  // AND_Gate
  Multiplexer #(.width(2)) multiplexer_2 (.in0(IM_data_2), .in1(IM_data[3:2]), .out(multiplexer_2_out), .sel(LW_out));
  or WB (WB_out, LW_out, ADD_out);
  Demultiplexer #(.select(2)) demultiplexer_1 (
    .out0(demultiplexer_1_out0), .out1(demultiplexer_1_out1), .out2(demultiplexer_1_out2),
    .out3(demultiplexer_1_out3), .in(WB_out), .sel(multiplexer_2_out));
  Register #(.width(4)) register_1 (
    .D(multiplexer_5_out), .en(demultiplexer_1_out0), .clk(clock_1_out), .Q(register_1_q), .clr(Reset_out));
  Register #(.width(4)) register_2 (
    .D(multiplexer_5_out), .en(demultiplexer_1_out1), .clk(clock_1_out), .Q(register_2_q), .clr(Reset_out));
  Register #(.width(4)) register_3 (
    .D(multiplexer_5_out), .en(demultiplexer_1_out2), .clk(clock_1_out), .Q(register_3_q), .clr(Reset_out));
  Register #(.width(4)) register_4 (
    .D(multiplexer_5_out), .en(demultiplexer_1_out3), .clk(clock_1_out), .Q(register_4_q), .clr(Reset_out));
  Multiplexer #(.select(2), .width(4)) multiplexer_3 (
    .in0(register_1_q), .in1(register_2_q), .in2(register_3_q), .in3(register_4_q), .out(multiplexer_3_out),
    .sel(IM_data[5:4]));
  Multiplexer #(.select(2), .width(4)) multiplexer_4 (
    .in0(register_1_q), .in1(register_2_q), .in2(register_3_q), .in3(register_4_q), .out(multiplexer_4_out),
    .sel(IM_data[3:2]));
  Multiplexer #(.width(4)) multiplexer_5 (
    .in0(fourbitadder_1_s0), .in1(MEM_dout), .out(multiplexer_5_out), .sel(LW_out));
  Multiplexer #(.width(4)) multiplexer_6 (
    .in0(multiplexer_4_out), .in1(not_2_out), .out(multiplexer_6_out), .sel(BEQ_out));
  assign not_2_out = ~multiplexer_4_out;  // NOT_Gate not_2, 4 bits wide
  or Imediato (Imediato_out, SW_out, LW_out);
  Multiplexer #(.width(4)) multiplexer_7 (
    .in0(multiplexer_6_out), .in1({2'b00, IM_data_2}), .out(multiplexer_7_out), .sel(Imediato_out));
  FourBitAdder fourbitadder_1 (
    .B3(multiplexer_7_out[3]), .A3(multiplexer_3_out[3]), .B2(multiplexer_7_out[2]),
    .A2(multiplexer_3_out[2]), .B1(multiplexer_7_out[1]), .A1(multiplexer_3_out[1]),
    .B0(multiplexer_7_out[0]), .A0(multiplexer_3_out[0]), .Cin(BEQ_out), .S3(fourbitadder_1_s0[3]),
    .S2(fourbitadder_1_s0[2]), .S1(fourbitadder_1_s0[1]), .S0(fourbitadder_1_s0[0]),
    .Overflow(fourbitadder_1_overflow), .Zero(fourbitadder_1_zero));
  RAM #(.addrWidth(4), .dataWidth(4), .trigger("falling")) MEM (
    .addr(fourbitadder_1_s0), .we(SW_out), .oe(LW_out), .clk(clock_1_out), .din(multiplexer_4_out),
    .dout(MEM_dout));
  LED led_1 (.in(fourbitadder_1_overflow));
  LED led_2 (.in(fourbitadder_1_zero));

  // Notes on the sheet:
  //   contents of IM (hex, n*v repeats v):
  //   87 88 18 cb 19 47 b 7
endmodule

module FullAdder (
  input  A,
  input  B,
  input  Cin,
  output S,
  output Cout
);

  wire and_1_out, and_2_out, xor_1_out;

  xor xor_1 (xor_1_out, A, B);
  xor xor_2 (S, xor_1_out, Cin);
  and and_1 (and_1_out, Cin, xor_1_out);
  and and_2 (and_2_out, B, A);
  or or_1 (Cout, and_1_out, and_2_out);
endmodule

module FourBitAdder (
  input  B3,
  input  A3,
  input  B2,
  input  A2,
  input  B1,
  input  A1,
  input  B0,
  input  A0,
  input  Cin,
  output S3,
  output S2,
  output S1,
  output S0,
  output Overflow,
  output Zero
);

  wire fulladder_1_cout, fulladder_2_cout, fulladder_3_cout, fulladder_4_cout;

  FullAdder fulladder_1 (.A(A3), .B(B3), .Cin(fulladder_2_cout), .S(S3), .Cout(fulladder_1_cout));
  xor xor_1 (Overflow, fulladder_1_cout, fulladder_2_cout);
  FullAdder fulladder_2 (.A(A2), .B(B2), .Cin(fulladder_3_cout), .S(S2), .Cout(fulladder_2_cout));
  and and_1 (Zero, ~S3, ~S2, ~S1, ~S0);  // AND_Gate
  FullAdder fulladder_3 (.A(A1), .B(B1), .Cin(fulladder_4_cout), .S(S1), .Cout(fulladder_3_cout));
  FullAdder fulladder_4 (.A(A0), .B(B0), .Cin(Cin), .S(S0), .Cout(fulladder_4_cout));
endmodule
